# Fritzing sketch enc28j60 (saved by Fritzing 0.9.2b)
circuit board: 4.40476cm x 5.84116cm
breadboards: 1

parts:
  Sensor = female alternating pin header, 3 pins [form="♀ (female)"]
  Fonte = male pin header, 2 pins [form="♂ (male)"]
  Arduino = Arduino Nano (Rev3.0)
  Sensor1 = female alternating pin header, 5 pins [form="♀ (female)"]
  Sensor2 = female alternating pin header, 5 pins [form="♀ (female)"]

nets:
  N1: Sensor.pin1, Fonte.pin1, Arduino.GND, Sensor2.pin1
  N2: Sensor.pin2, Arduino.D3
  N3: Sensor.pin3, Arduino.5V, Sensor1.pin1
  N4: Fonte.pin2, Arduino.VIN
  N5: Arduino.D2, Sensor2.pin5
  N6: Arduino.D10, Sensor1.pin2
  N7: Arduino.D11/MOSI, Sensor1.pin3
  N8: Arduino.D12/MISO, Sensor2.pin4
  N9: Arduino.D13/SCK, Sensor2.pin3
